// Logisim project Logisim 3 bit mux.circ as structural Verilog: 1 circuit, main circuit Output0
module Output0 (
  input  Select0,
  input  Select1,
  input  Select2,
  input  Input0,
  input  Input1,
  input  Input2,
  input  Input3,
  input  Input4,
  input  Input5,
  input  Input6,
  input  Input7,
  output Output0
);

  wire and_1_out, and_2_out, and_3_out, and_4_out, and_5_out, and_6_out, and_7_out, and_8_out, not_1_out,
       not_2_out, not_3_out;

  not not_1 (not_1_out, Select0);
  not not_2 (not_2_out, Select1);
  not not_3 (not_3_out, Select2);
  and and_1 (and_1_out, Input0, not_1_out, not_2_out, not_3_out);
  and and_2 (and_2_out, Input1, not_1_out, not_2_out, Select2);
  and and_3 (and_3_out, Input2, not_1_out, Select1, not_3_out);
  and and_4 (and_4_out, Input3, not_1_out, Select1, Select2);
  and and_5 (and_5_out, Input4, Select0, not_2_out, not_3_out);
  and and_6 (and_6_out, Input5, Select0, not_2_out, Select2);
  and and_7 (and_7_out, Input6, Select0, Select1, not_3_out);
  and and_8 (and_8_out, Input7, Select0, Select1, Select2);
  or or_1 (Output0, and_1_out, and_2_out, and_3_out, and_4_out, and_5_out, and_6_out, and_7_out, and_8_out);
endmodule
