// Logisim project Logisim 4 bit register.circ as structural Verilog: 1 circuit, main circuit main
module main (
  input  Right_Left_shift,
  input  in_2,
  input  in_3,
  input  Clock,
  input  Reset,
  output [3:0] out_6,
  output out_7,
  output out_8
);

  wire and_1_out, and_2_out, and_3_out, and_4_out, and_5_out, and_6_out, and_7_out, and_8_out, not_1_out,
       or_1_out, or_2_out, or_3_out, or_4_out;

  not not_1 (not_1_out, Right_Left_shift);
  and and_1 (and_1_out, out_6[1], Right_Left_shift);
  and and_2 (and_2_out, in_2, not_1_out);
  or or_1 (or_1_out, and_1_out, and_2_out);
  D_Flip_Flop d_ff_1 (.clk(Clock), .D(or_1_out), .Q(out_6[0]), .reset(Reset));  // open: Qn, preset, en
  and and_3 (and_3_out, out_6[2], Right_Left_shift);
  and and_4 (and_4_out, out_6[0], not_1_out);
  or or_2 (or_2_out, and_3_out, and_4_out);
  D_Flip_Flop d_ff_2 (.clk(Clock), .D(or_2_out), .Q(out_6[1]), .reset(Reset));  // open: Qn, preset, en
  and and_5 (and_5_out, out_6[3], Right_Left_shift);
  and and_6 (and_6_out, out_6[1], not_1_out);
  or or_3 (or_3_out, and_5_out, and_6_out);
  D_Flip_Flop d_ff_3 (.clk(Clock), .D(or_3_out), .Q(out_6[2]), .reset(Reset));  // open: Qn, preset, en
  and and_7 (and_7_out, in_3, Right_Left_shift);
  and and_8 (and_8_out, out_6[2], not_1_out);
  or or_4 (or_4_out, and_7_out, and_8_out);
  D_Flip_Flop d_ff_4 (.clk(Clock), .D(or_4_out), .Q(out_6[3]), .reset(Reset));  // open: Qn, preset, en

  assign out_7 = out_6[3];
  assign out_8 = out_6[0];

  // Notes on the sheet:
  //   Data input in left shift
  //   Data input in right shift
  //   LSB
  //   Current State of the Registers
  //   MSB
  //   Data in the Left Shift
  //   Data out in the Right Shift
endmodule
