// Logisim project Logisim error.circ as structural Verilog: 1 circuit, main circuit main
module main (
  input  in_1,
  input  in_2,
  input  in_3,
  input  in_4,
  input  in_5,
  input  in_6,
  input  in_7,
  input  in_8,
  input  in_9,
  input  in_10,
  input  in_11,
  output out_12,
  output out_13,
  output out_14,
  output out_15,
  output out_16,
  output out_17,
  output out_18,
  output out_19,
  output out_20,
  output out_21,
  output out_22,
  output out_23,
  output out_24,
  output out_25,
  output out_26
);

  wire xor_1_out, xor_2_out, xor_3_out, xor_4_out, xor_5_out, xor_6_out, xor_7_out, xor_8_out;

  // XOR_Gate xor_1 has open pins: out=xor_1_out
  xor xor_2 (xor_2_out, in_1, in_2);
  buf xor_3 (xor_3_out, in_1);  // XOR_Gate
  // XOR_Gate xor_4 has open pins: out=xor_4_out
  ExactlyOne xor_5 (.out(xor_5_out), .in0(xor_2_out), .in2(in_5), .in3(in_7));
  buf xor_6 (xor_6_out, xor_3_out);  // XOR_Gate
  buf xor_7 (xor_7_out, xor_4_out);  // XOR_Gate
  buf xor_8 (xor_8_out, xor_1_out);  // XOR_Gate
  ExactlyOne xor_9 (.out(out_12), .in0(xor_5_out), .in1(in_9), .in2(in_11));
  buf xor_10 (out_13, xor_6_out);  // XOR_Gate
  buf xor_11 (out_14, xor_7_out);  // XOR_Gate
  buf xor_12 (out_15, xor_8_out);  // XOR_Gate
  // XOR_Gate xor_13 is placed but not wired
  // XOR_Gate xor_14 is placed but not wired
  // XOR_Gate xor_15 is placed but not wired
  // XOR_Gate xor_16 is placed but not wired
  // XOR_Gate xor_17 is placed but not wired
  // XOR_Gate xor_18 is placed but not wired
  // XOR_Gate xor_19 is placed but not wired
  // XOR_Gate xor_20 is placed but not wired
  // XOR_Gate xor_21 is placed but not wired
  // XOR_Gate xor_22 is placed but not wired
  // XOR_Gate xor_23 is placed but not wired
  // XOR_Gate xor_24 is placed but not wired

  assign out_16 = in_1;
  assign out_17 = in_2;
  assign out_18 = in_3;
  assign out_19 = in_4;
  assign out_20 = in_5;
  assign out_21 = in_6;
  assign out_22 = in_7;
  assign out_23 = in_8;
  assign out_24 = in_9;
  assign out_25 = in_10;
  assign out_26 = in_11;

  // Notes on the sheet:
  //   Parity 0 Group: Data: 0,1,3,4,6,8,10
  //   Parity 1 Group: Data: 0,2 3,5,6,9,10 
  //   Parity 2 Group: Data: 1,2,3,7,8,9,10
  //   Parity 3 Group: Data: 4,5,6,7,8,9,10
endmodule
