// Logisim project Logisim 3 bit decoder.circ as structural Verilog: 1 circuit, main circuit main
module main (
  input  Select0,
  input  Select1,
  input  Select2,
  output Output0,
  output Output1,
  output Output2,
  output Output3,
  output Output4,
  output Output5,
  output Output6,
  output Output7
);

  wire not_1_out, not_2_out, not_3_out;

  not not_1 (not_1_out, Select0);
  not not_2 (not_2_out, Select1);
  not not_3 (not_3_out, Select2);
  and and_1 (Output0, not_3_out, not_2_out, not_1_out);
  and and_2 (Output1, Select2, not_2_out, not_1_out);
  and and_3 (Output2, not_3_out, Select1, not_1_out);
  and and_4 (Output3, Select2, Select1, not_1_out);
  and and_5 (Output4, not_3_out, not_2_out, Select0);
  and and_6 (Output5, Select2, not_2_out, Select0);
  and and_7 (Output6, not_3_out, Select1, Select0);
  and and_8 (Output7, Select2, Select1, Select0);
endmodule
