// Logisim project Logisim 4 bit full adder.circ as structural Verilog: 1 circuit, main circuit main
module main (
  input  A_Operand_0,
  input  in_2,
  input  CarryIn_0,
  input  A_Operand_1,
  input  B_Operand_1,
  input  A_Operand_2,
  input  B_Operand_2,
  input  A_Operand_3,
  input  B_Operand_3,
  output Sum_0,
  output Sum_1,
  output Sum_2,
  output Sum_3,
  output CarryOut_3
);

  wire and_1_out, and_2_out, and_3_out, and_4_out, and_5_out, and_6_out, and_7_out, and_8_out, xor_1_out,
       xor_2_out, xor_3_out, xor_4_out, xor_9_out, xor_10_out, xor_11_out;

  xor xor_1 (xor_1_out, A_Operand_0, in_2);
  xor xor_2 (xor_2_out, A_Operand_1, B_Operand_1);
  xor xor_3 (xor_3_out, A_Operand_2, B_Operand_2);
  xor xor_4 (xor_4_out, A_Operand_3, B_Operand_3);
  and and_1 (and_1_out, CarryIn_0, xor_1_out);
  and and_2 (and_2_out, in_2, A_Operand_0);
  and and_3 (and_3_out, xor_9_out, xor_2_out);
  and and_4 (and_4_out, B_Operand_1, A_Operand_1);
  and and_5 (and_5_out, xor_10_out, xor_3_out);
  and and_6 (and_6_out, B_Operand_2, A_Operand_2);
  and and_7 (and_7_out, xor_11_out, xor_4_out);
  and and_8 (and_8_out, B_Operand_3, A_Operand_3);
  xor xor_5 (Sum_0, xor_1_out, CarryIn_0);
  xor xor_6 (Sum_1, xor_2_out, xor_9_out);
  xor xor_7 (Sum_2, xor_3_out, xor_10_out);
  xor xor_8 (Sum_3, xor_4_out, xor_11_out);
  xor xor_9 (xor_9_out, and_1_out, and_2_out);
  xor xor_10 (xor_10_out, and_3_out, and_4_out);
  xor xor_11 (xor_11_out, and_5_out, and_6_out);
  xor xor_12 (CarryOut_3, and_7_out, and_8_out);

  // Notes on the sheet:
  //   B-Operand-0
  //   CarryOut-0
  //   CarryOut-1
  //   CarryOut-2
endmodule
