// Logisim project Logisim Error Detection_Correction.circ as structural Verilog: 1 circuit, main circuit main
module main (
  input  in_1,
  input  in_2,
  input  in_3,
  input  in_4,
  input  in_5,
  input  in_6,
  input  in_7,
  input  in_8,
  input  in_9,
  input  in_10,
  input  in_11,
  output Parity_0,
  output Parity_1,
  output Parity_2,
  output Parity_3,
  output Data_0,
  output Data_1,
  output Data_2,
  output Data_3,
  output Data_4,
  output Data_5,
  output Data_6,
  output Data_7,
  output Data_8,
  output Data_9,
  output Data_10
);

  wire xor_1_out, xor_2_out, xor_3_out, xor_4_out, xor_5_out, xor_7_out, xor_8_out, xor_9_out, xor_10_out,
       xor_11_out, xor_13_out, xor_14_out, xor_15_out, xor_16_out, xor_17_out, xor_19_out, xor_20_out,
       xor_21_out, xor_22_out, xor_23_out;

  xor xor_1 (xor_1_out, in_1, in_2);
  xor xor_2 (xor_2_out, xor_1_out, in_4);
  xor xor_3 (xor_3_out, xor_2_out, in_5);
  xor xor_4 (xor_4_out, xor_3_out, in_7);
  xor xor_5 (xor_5_out, xor_4_out, in_9);
  xor xor_6 (Parity_0, xor_5_out, in_11);
  xor xor_7 (xor_7_out, in_1, in_3);
  xor xor_8 (xor_8_out, xor_7_out, in_4);
  xor xor_9 (xor_9_out, xor_8_out, in_6);
  xor xor_10 (xor_10_out, xor_9_out, in_7);
  xor xor_11 (xor_11_out, xor_10_out, in_10);
  xor xor_12 (Parity_1, xor_11_out, in_11);
  xor xor_13 (xor_13_out, in_2, in_3);
  xor xor_14 (xor_14_out, xor_13_out, in_4);
  xor xor_15 (xor_15_out, xor_14_out, in_8);
  xor xor_16 (xor_16_out, xor_15_out, in_9);
  xor xor_17 (xor_17_out, xor_16_out, in_10);
  xor xor_18 (Parity_2, xor_17_out, in_11);
  xor xor_19 (xor_19_out, in_5, in_6);
  xor xor_20 (xor_20_out, xor_19_out, in_7);
  xor xor_21 (xor_21_out, xor_20_out, in_8);
  xor xor_22 (xor_22_out, xor_21_out, in_9);
  xor xor_23 (xor_23_out, xor_22_out, in_10);
  xor xor_24 (Parity_3, xor_23_out, in_11);

  assign Data_0 = in_1;
  assign Data_1 = in_2;
  assign Data_2 = in_3;
  assign Data_3 = in_4;
  assign Data_4 = in_5;
  assign Data_5 = in_6;
  assign Data_6 = in_7;
  assign Data_7 = in_8;
  assign Data_8 = in_9;
  assign Data_9 = in_10;
  assign Data_10 = in_11;

  // Notes on the sheet:
  //   Parity 0 Group: Data: 0,1,3,4,6,8,10
  //   Parity 1 Group: Data: 0,2 3,5,6,9,10 
  //   Parity 2 Group: Data: 1,2,3,7,8,9,10
  //   Parity 3 Group: Data: 4,5,6,7,8,9,10
endmodule
